// Logisim project controller.circ as structural Verilog: 1 circuit, main circuit controller
module controller (
  input  start,
  input  ar_ready,
  input  r_valid,
  input  r_resp,
  input  write_submodule_done,
  input  write_submodule_b_resp,
  input  elem2insert_gt_elem2compare,
  input  j_gte_0,
  input  i_lt_arr_size,
  input  clk,
  input  rst_n,
  output done,
  output sl_incd_to_i,
  output ld_return_read_data,
  output error,
  output ld_i,
  output sl_j_plus_1_to_write_addr,
  output sl_elem2compare_to_write_data,
  output ar_valid,
  output sl_decrd_to_j,
  output write_submodule_start,
  output r_ready,
  output ld_j,
  output ld_elem2insert,
  output ld_elem2compare,
  output sl_j_to_arg_read_addr,
  output ld_arg_read_addr
);

  wire and_1_out, and_2_out, and_3_out, and_8_out, and_9_out, and_10_out, and_11_out, and_12_out, assign_i,
       assng_j, check_if_correct_place, complete_ar, gen_assign_i, gen_complete_ar, gen_decrmt_j, gen_done,
       gen_err, gen_inc_i, gen_outer_loop_check, gen_process_r_data_resp, gen_read_arr_i, gen_read_arr_j,
       gen_read_function, gen_return_read_fn, gen_shif_elem2compare_right, gen_shift_elem2insert_left,
       ld_arg_return_state, not_1_out, sl_to_arg_return_state;
  wire [0:0] multiplexer_1_out;
  wire [4:0] arg_return_state_q, d_arg_return_state;
  wire [20:0] gen_state;
  wire [22:0] current_state, multiplexer_1_out_2;
  wire [23:0] decoder_1_out0;

  not not_1 (not_1_out, rst_n);
  and and_1 (and_1_out, current_state[2], ~i_lt_arr_size);  // AND_Gate
  and and_2 (and_2_out, current_state[7], ~j_gte_0);  // AND_Gate
  and and_3 (and_3_out, check_if_correct_place, elem2insert_gt_elem2compare);
  or or_1 (ar_valid, current_state[17], current_state[18]);
  or or_2 (r_ready, complete_ar, current_state[20]);
  and and_4 (gen_state[0], current_state[0], ~start);  // AND_Gate
  and and_5 (gen_assign_i, current_state[0], start);
  or or_3 (gen_outer_loop_check, assign_i, sl_incd_to_i);
  or or_4 (gen_done, and_1_out, done);
  and and_6 (gen_read_arr_i, current_state[2], i_lt_arr_size);
  or or_5 (gen_inc_i, and_2_out, and_3_out, sl_decrd_to_j);
  and and_7 (gen_read_arr_j, current_state[7], j_gte_0);
  Register #(.width(5)) arg_return_state (
    .D(d_arg_return_state), .en(ld_arg_return_state), .clk(clk), .Q(arg_return_state_q), .clr(not_1_out));
  or or_6 (ld_i, sl_incd_to_i, assign_i);
  or or_7 (ld_j, sl_decrd_to_j, assng_j);
  or or_8 (ld_arg_read_addr, current_state[4], sl_j_to_arg_read_addr);
  Decoder #(.enable("false"), .select(5)) decoder_1 (
    .out0(decoder_1_out0[0]), .out1(decoder_1_out0[1]), .out2(decoder_1_out0[2]), .out3(decoder_1_out0[3]),
    .out4(decoder_1_out0[4]), .out5(decoder_1_out0[5]), .out6(decoder_1_out0[6]), .out7(decoder_1_out0[7]),
    .out8(decoder_1_out0[8]), .out9(decoder_1_out0[9]), .out10(decoder_1_out0[10]),
    .out11(decoder_1_out0[11]), .out12(decoder_1_out0[12]), .out13(decoder_1_out0[13]),
    .out14(decoder_1_out0[14]), .out15(decoder_1_out0[15]), .out16(decoder_1_out0[16]),
    .out17(decoder_1_out0[17]), .out18(decoder_1_out0[18]), .out19(decoder_1_out0[19]),
    .out20(decoder_1_out0[20]), .out21(decoder_1_out0[21]), .out22(decoder_1_out0[22]),
    .out23(decoder_1_out0[23]), .sel(arg_return_state_q));  // open: out24, out25, out26, out27, out28, out29, out30, out31
  Multiplexer #(.width(24)) multiplexer_1 (
    .in0({gen_err, gen_return_read_fn, gen_process_r_data_resp, gen_state[20], gen_complete_ar, gen_state[18], gen_read_function, gen_decrmt_j, gen_state[15], gen_shif_elem2compare_right, gen_state[13], gen_shift_elem2insert_left, ld_elem2compare, 1'b0, gen_read_arr_j, gen_inc_i, assng_j, ld_elem2insert, 1'b0, gen_read_arr_i, gen_done, gen_outer_loop_check, gen_assign_i, gen_state[0]}),
    .in1(decoder_1_out0), .out({multiplexer_1_out_2, multiplexer_1_out[0]}), .sel(current_state[22]));
  and and_8 (and_8_out, current_state[18], ~ar_ready);  // AND_Gate
  and and_9 (and_9_out, current_state[20], ~r_valid);  // AND_Gate
  and and_10 (and_10_out, ld_return_read_data, ~r_resp);  // AND_Gate
  and and_11 (and_11_out, gen_shif_elem2compare_right, ~write_submodule_b_resp);  // AND_Gate
  and and_12 (and_12_out, gen_decrmt_j, ~write_submodule_b_resp);  // AND_Gate
  Register #(.width(23)) register_1 (
    .D(multiplexer_1_out_2), .en(1'b1), .clk(clk),
    .Q({error, current_state[22], ld_return_read_data, current_state[20], complete_ar, current_state[18:17], sl_decrd_to_j, current_state[15], sl_elem2compare_to_write_data, current_state[13:12], check_if_correct_place, ld_elem2compare, sl_j_to_arg_read_addr, sl_incd_to_i, current_state[7], assng_j, ld_elem2insert, current_state[4], done, current_state[2], assign_i}),
    .clr(not_1_out));
  and and_13 (gen_shift_elem2insert_left, check_if_correct_place, ~elem2insert_gt_elem2compare);  // AND_Gate
  or or_9 (gen_read_function, current_state[4], sl_j_to_arg_read_addr);
  or or_10 (gen_state[18], current_state[17], and_8_out);
  and and_14 (gen_complete_ar, current_state[18], ar_ready);
  or or_11 (gen_state[20], complete_ar, and_9_out);
  and and_15 (gen_process_r_data_resp, current_state[20], r_valid);
  and and_16 (gen_return_read_fn, ld_return_read_data, r_resp);
  or or_12 (gen_err, and_10_out, and_11_out, and_12_out);
  D_Flip_Flop d_ff_1 (
    .D(multiplexer_1_out[0]), .clk(clk), .Q(current_state[0]), .preset(not_1_out), .reset(1'b0));  // open: Qn
  or or_13 (write_submodule_start, current_state[12], sl_elem2compare_to_write_data);
  Multiplexer #(.width(5)) multiplexer_2 (
    .in0(5'b00101), .in1(5'b01010), .out(d_arg_return_state), .sel(sl_to_arg_return_state));
  and and_17 (gen_state[13], current_state[13], ~write_submodule_done);  // AND_Gate
  and and_18 (gen_shif_elem2compare_right, current_state[13], write_submodule_done);
  and and_19 (gen_state[15], current_state[15], ~write_submodule_done);  // AND_Gate
  and and_20 (gen_decrmt_j, current_state[15], write_submodule_done);
  or or_14 (ld_arg_return_state, current_state[4], sl_j_to_arg_read_addr);
  Priority_Encoder #(.select(1)) priority_encoder_1 (
    .in0(current_state[4]), .in1(sl_j_to_arg_read_addr), .out(sl_to_arg_return_state),
    .en_in(ld_arg_return_state));  // open: gs, en_out

  assign sl_j_plus_1_to_write_addr = sl_elem2compare_to_write_data;

  // Other names for the same wires on the sheet: wait_start = current_state[0];
  //   current_state (some bits) = {error, ld_return_read_data, complete_ar, sl_decrd_to_j, sl_elem2compare_to_write_data, check_if_correct_place, ld_elem2compare, sl_j_to_arg_read_addr, sl_incd_to_i, assng_j, ld_elem2insert, done, assign_i};
  //   outer_loop_check = current_state[2]; read_arr_i = current_state[4]; assign_elem2insert = ld_elem2insert;
  //   gen_assng_j = ld_elem2insert;
  //   gen_state (some bits) = {gen_err, gen_return_read_fn, gen_process_r_data_resp, gen_complete_ar, gen_read_function, gen_decrmt_j, gen_shif_elem2compare_right, gen_shift_elem2insert_left, ld_elem2compare, gen_read_arr_j, gen_inc_i, assng_j, ld_elem2insert, gen_read_arr_i, gen_done, gen_outer_loop_check, gen_assign_i};
  //   gen_inner_loop_check = assng_j; inner_loop_check = current_state[7]; inc_i = sl_incd_to_i;
  //   read_arr_j = sl_j_to_arg_read_addr; assign_elem2compare = ld_elem2compare;
  //   gen_check_if_correct_place = ld_elem2compare; shift_elem2insert_left = current_state[12];
  //   wait_submodule_return1 = current_state[13]; shif_elem2compare_right = sl_elem2compare_to_write_data;
  //   wait_submodule_return2 = current_state[15]; decrmt_j = sl_decrd_to_j; read_function = current_state[17];
  //   wait_ar_ready = current_state[18]; wait_r_valid = current_state[20]; process_r_data_resp = ld_return_read_data;
  //   return_read_fn = current_state[22]; sl_to_state = current_state[22]; err = error;
  //   e2ins_gt_e2cmp = elem2insert_gt_elem2compare; gen_wait_start = gen_state[0];
  //   gen_wait_submodule_return1 = gen_state[13]; gen_wait_submodule_return2 = gen_state[15];
  //   gen_wait_ar_ready = gen_state[18]; gen_wait_r_valid = gen_state[20]

  // Notes on the sheet:
  //   Output Generation
  //   Next State Generation
  //   onehot encoding
  //   those states reached via function return
  //   Internal Control Signal Generation
endmodule
